# Fritzing sketch Circuitry Sketch (saved by Fritzing 0.9.10b)

parts:
  Mod1 = Raspberry Pi 4B
  Disp4 = 60mm 8x8 dot matrix column cathode led display with standard pcb pads  # not connected
  Disp5 = 60mm 8x8 dot matrix column cathode led display with standard pcb pads  # not connected
  Disp7 = 60mm 8x8 dot matrix column cathode led display with standard pcb pads  # not connected
  Disp6 = 60mm 8x8 dot matrix column cathode led display with standard pcb pads  # not connected
  part = SO-24x [chip_label=SO-24x package=SO(x)]  # not connected
  5V_2A_DC_Power_Supply = Power plug

nets:
  GND: Mod1.GND, 5V_2A_DC_Power_Supply.GND

notes:
  Vcc+
  GND
  GPIO18
  DIN
  WS2812B 16 x 16 LED Matrix
  Raspberry Pi 4 Model B
  5V, 2A Power Supply
